// Logisim project registers.circ as structural Verilog: 3 circuits, main circuit alu
module alu (
  input  F2,
  input  F1,
  input  F0,
  input  [15:0] A,
  input  [15:0] B,
  output [15:0] Y
);

  wire [15:0] adder_1_out, and_1_out, bit_extender_1_out, multiplexer_1_out, not_1_out, or_1_out;

  assign not_1_out = ~B;  // NOT_Gate not_1, 16 bits wide
  Multiplexer #(.width(16)) multiplexer_1 (.in0(B), .in1(not_1_out), .out(multiplexer_1_out), .sel(F2));
  Adder #(.width(16)) adder_1 (.a(A), .b(multiplexer_1_out), .out(adder_1_out), .cin(F2));  // open: cout
  assign and_1_out = A & multiplexer_1_out;  // AND_Gate and_1, 16 bits wide
  assign or_1_out = A | multiplexer_1_out;  // OR_Gate or_1, 16 bits wide
  assign bit_extender_1_out = {{15{1'b0}}, adder_1_out[15]};  // Bit_Extender bit_extender_1
  Multiplexer #(.select(2), .width(16)) multiplexer_2 (
    .in0(and_1_out), .in1(or_1_out), .in2(adder_1_out), .in3(bit_extender_1_out), .out(Y), .sel({F1, F0}));
endmodule

module registers1 (
);

  wire [15:0] alu_1_y;
  wire [34:0] rom_1_data;

  ROM #(.addrWidth(3), .dataWidth(35)) rom_1 (.addr(3'b101), .data(rom_1_data));
  // Probe on rom_1_data[34:19]
  // Probe on rom_1_data[18:3]
  // Probe on rom_1_data[2:0]
  // Probe on alu_1_y
  alu alu_1 (
    .A(rom_1_data[34:19]), .B(rom_1_data[18:3]), .F2(rom_1_data[2]), .F1(rom_1_data[1]), .F0(rom_1_data[0]),
    .Y(alu_1_y));

  // Notes on the sheet:
  //   contents of rom_1 (hex, n*v repeats v):
  //   8000a 57fffa 50000e 10000f 80017
endmodule

module registers2 (
);

  wire clock_1_out, RESET_out;
  wire [2:0] counter_1_q;
  wire [15:0] A_q, alu_1_y, B_q, multiplexer_1_out;
  wire [37:0] rom_1_data;

  Clock clock_1 (.out(clock_1_out));
  Button RESET (.out(RESET_out));
  Counter #(.max('h7), .width(3)) counter_1 (
    .clr(RESET_out), .clk(clock_1_out), .Q(counter_1_q));  // open: load, up, count, D, carry
  ROM #(.addrWidth(3), .dataWidth(38)) rom_1 (.addr(counter_1_q), .data(rom_1_data));
  Multiplexer #(.width(16)) multiplexer_1 (
    .in0(rom_1_data[37:22]), .in1(alu_1_y), .out(multiplexer_1_out), .sel(rom_1_data[20]));
  Register #(.width(16)) A (.D(multiplexer_1_out), .en(rom_1_data[21]), .clk(clock_1_out), .Q(A_q));  // open: clr
  Register #(.width(16)) B (.D(rom_1_data[19:4]), .en(rom_1_data[3]), .clk(clock_1_out), .Q(B_q));  // open: clr
  // Probe on alu_1_y
  // Probe on rom_1_data[2:0]
  // Probe on A_q
  // Probe on B_q
  alu alu_1 (.A(A_q), .B(B_q), .F2(rom_1_data[2]), .F1(rom_1_data[1]), .F0(rom_1_data[0]), .Y(alu_1_y));

  // Notes on the sheet:
  //   contents of rom_1 (hex, n*v repeats v):
  //   e00038 300002 300002 300002
endmodule
