// Logisim project JZ.circ as structural Verilog: 5 circuits, main circuit main
module alu (
  input  F2,
  input  F1,
  input  F0,
  input  [15:0] A,
  input  [15:0] B,
  output [15:0] Y
);

  wire [15:0] adder_1_out, and_1_out, bit_extender_1_out, multiplexer_1_out, not_1_out, or_1_out;

  assign not_1_out = ~B;  // NOT_Gate not_1, 16 bits wide
  Multiplexer #(.width(16)) multiplexer_1 (.in0(B), .in1(not_1_out), .out(multiplexer_1_out), .sel(F2));
  Adder #(.width(16)) adder_1 (.a(A), .b(multiplexer_1_out), .out(adder_1_out), .cin(F2));  // open: cout
  assign and_1_out = A & multiplexer_1_out;  // AND_Gate and_1, 16 bits wide
  assign or_1_out = A | multiplexer_1_out;  // OR_Gate or_1, 16 bits wide
  assign bit_extender_1_out = {{15{1'b0}}, adder_1_out[15]};  // Bit_Extender bit_extender_1
  Multiplexer #(.select(2), .width(16)) multiplexer_2 (
    .in0(and_1_out), .in1(or_1_out), .in2(adder_1_out), .in3(bit_extender_1_out), .out(Y), .sel({F1, F0}));
endmodule

module control_unit (
  input  [3:0] OP_CODE,
  output WE_A,
  output WE_B,
  output SRC_A,
  output [2:0] ALU_OP_CODE,
  output PC_LOAD
);

  ROM #(.addrWidth(4), .dataWidth(7)) ControlROM (.addr(OP_CODE), .data({WE_A, WE_B, SRC_A, ALU_OP_CODE, PC_LOAD}));

  // Notes on the sheet:
  //   contents of ControlROM (hex, n*v repeats v):
  //   0 40 20 50 52 54 58 5a 5c 5e 1
endmodule

module main (
);

  wire clock_1_out, control_unit_1_src_a, control_unit_1_we_a, control_unit_1_we_b, PC_LOAD, RESET_out;
  wire [2:0] control_unit_1_alu_op_code, counter_1_q;
  wire [15:0] A_q, alu_1_y, B_q, multiplexer_1_out;
  wire [19:0] ProgramROM_data;

  Button RESET (.out(RESET_out));
  Clock clock_1 (.out(clock_1_out));
  ROM #(.addrWidth(3), .dataWidth(20)) ProgramROM (.addr(counter_1_q), .data(ProgramROM_data));
  Counter #(.max('h7), .width(3)) counter_1 (
    .clr(RESET_out), .load(PC_LOAD), .clk(clock_1_out), .Q(counter_1_q));  // open: up, count, D, carry
  // Probe on ProgramROM_data[15:0]
  // Probe on control_unit_1_we_a
  Multiplexer #(.width(16)) multiplexer_1 (
    .in0(ProgramROM_data[15:0]), .in1(alu_1_y), .out(multiplexer_1_out), .sel(control_unit_1_src_a));
  control_unit control_unit_1 (
    .OP_CODE(ProgramROM_data[19:16]), .WE_A(control_unit_1_we_a), .WE_B(control_unit_1_we_b),
    .SRC_A(control_unit_1_src_a), .ALU_OP_CODE(control_unit_1_alu_op_code), .PC_LOAD(PC_LOAD));
  Register #(.width(16)) A (.D(multiplexer_1_out), .en(control_unit_1_we_a), .clk(clock_1_out), .Q(A_q));  // open: clr
  Register #(.width(16)) B (
    .D(ProgramROM_data[15:0]), .en(control_unit_1_we_b), .clk(clock_1_out), .Q(B_q));  // open: clr
  // Probe on alu_1_y
  // Probe on A_q
  // Probe on B_q
  // Probe on control_unit_1_alu_op_code
  alu alu_1 (
    .A(A_q), .B(B_q), .F2(control_unit_1_alu_op_code[2]), .F1(control_unit_1_alu_op_code[1]),
    .F0(control_unit_1_alu_op_code[0]), .Y(alu_1_y));

  // Notes on the sheet:
  //   contents of ProgramROM (hex, n*v repeats v):
  //   10003 20003 50000 50000
endmodule

module jz (
);

  wire clock_1_out, control_unit_1_pc_load, control_unit_1_src_a, control_unit_1_we_a, control_unit_1_we_b,
       jz_control_1_m1, RESET_out;
  wire [2:0] control_unit_1_alu_op_code;
  wire [15:0] A_q, alu_1_y, B_q, counter_1_q, multiplexer_1_out;
  wire [19:0] ProgramROM_data;

  Button RESET (.out(RESET_out));
  Clock clock_1 (.out(clock_1_out));
  Counter #(.max('hffff), .width(16)) counter_1 (
    .clr(RESET_out), .load(jz_control_1_m1), .clk(clock_1_out), .D(ProgramROM_data[15:0]), .Q(counter_1_q));  // open: up, count, carry
  ROM #(.addrWidth(16), .dataWidth(20)) ProgramROM (.addr(counter_1_q), .data(ProgramROM_data));
  // Probe on ProgramROM_data[15:0]
  // Probe on control_unit_1_we_a
  control_unit control_unit_1 (
    .OP_CODE(ProgramROM_data[19:16]), .WE_A(control_unit_1_we_a), .WE_B(control_unit_1_we_b),
    .SRC_A(control_unit_1_src_a), .ALU_OP_CODE(control_unit_1_alu_op_code), .PC_LOAD(control_unit_1_pc_load));
  Multiplexer #(.width(16)) multiplexer_1 (
    .in0(ProgramROM_data[15:0]), .in1(alu_1_y), .out(multiplexer_1_out), .sel(control_unit_1_src_a));
  Register #(.width(16)) A (.D(multiplexer_1_out), .en(control_unit_1_we_a), .clk(clock_1_out), .Q(A_q));  // open: clr
  Register #(.width(16)) B (
    .D(ProgramROM_data[15:0]), .en(control_unit_1_we_b), .clk(clock_1_out), .Q(B_q));  // open: clr
  // Probe on alu_1_y
  // Probe on control_unit_1_alu_op_code
  jz_control jz_control_1 (.A(A_q), .PC_LOAD(control_unit_1_pc_load), .M1(jz_control_1_m1));
  // Probe on A_q
  // Probe on B_q
  alu alu_1 (
    .A(A_q), .B(B_q), .F2(control_unit_1_alu_op_code[2]), .F1(control_unit_1_alu_op_code[1]),
    .F0(control_unit_1_alu_op_code[0]), .Y(alu_1_y));

  // Notes on the sheet:
  //   contents of ProgramROM (hex, n*v repeats v):
  //   20009 10001 30000 a0006 20001 a0007 20000
endmodule

module jz_control (
  input  [15:0] A,
  input  PC_LOAD,
  output M1
);

  wire comparator_1_eq;

  Comparator #(.width(16)) comparator_1 (.a(A), .b({16{1'b0}}), .eq(comparator_1_eq));  // open: gt, lt
  and and_1 (M1, comparator_1_eq, PC_LOAD);
endmodule
