// Logisim project RAM.circ as structural Verilog: 4 circuits, main circuit main
module alu (
  input  F2,
  input  F1,
  input  F0,
  input  [15:0] A,
  input  [15:0] B,
  output [15:0] Y
);

  wire [15:0] adder_1_out, and_1_out, bit_extender_1_out, multiplexer_1_out, not_1_out, or_1_out;

  assign not_1_out = ~B;  // NOT_Gate not_1, 16 bits wide
  Multiplexer #(.width(16)) multiplexer_1 (.in0(B), .in1(not_1_out), .out(multiplexer_1_out), .sel(F2));
  Adder #(.width(16)) adder_1 (.a(A), .b(multiplexer_1_out), .out(adder_1_out), .cin(F2));  // open: cout
  assign and_1_out = A & multiplexer_1_out;  // AND_Gate and_1, 16 bits wide
  assign or_1_out = A | multiplexer_1_out;  // OR_Gate or_1, 16 bits wide
  assign bit_extender_1_out = {{15{1'b0}}, adder_1_out[15]};  // Bit_Extender bit_extender_1
  Multiplexer #(.select(2), .width(16)) multiplexer_2 (
    .in0(and_1_out), .in1(or_1_out), .in2(adder_1_out), .in3(bit_extender_1_out), .out(Y), .sel({F1, F0}));
endmodule

module control_unit (
  input  [4:0] OP_CODE,
  output WE_A,
  output WE_B,
  output [1:0] SRC_A,
  output SRC_B,
  output [2:0] ALU_OP_CODE,
  output MEM_READ,
  output MEM_WRITE,
  output MEM_SRC,
  output MEM_ADDR_SRC,
  output PC_LOAD
);

  ROM #(.addrWidth(5), .dataWidth(13)) ControlROM (
    .addr(OP_CODE),
    .data({WE_A, WE_B, SRC_A, SRC_B, ALU_OP_CODE, MEM_READ, MEM_WRITE, MEM_SRC, MEM_ADDR_SRC, PC_LOAD}));

  // Notes on the sheet:
  //   OP_CODE: initial=0x44c
  //   contents of ControlROM (hex, n*v repeats v):
  //   0 1000 800 1200 1220 1240 1280 12a0 12c0 12e0 1 8 8 c 1410 b10 1412 a
endmodule

module main (
);

  wire clock_1_out, control_unit_1_mem_addr_src, control_unit_1_mem_read, control_unit_1_mem_src,
       control_unit_1_mem_write, control_unit_1_src_b, control_unit_1_we_a, control_unit_1_we_b,
       jz_control_1_m1, PC_LOAD, RESET_out;
  wire [1:0] control_unit_1_src_a;
  wire [2:0] control_unit_1_alu_op_code;
  wire [7:0] multiplexer_3_out, multiplexer_3_out_2;
  wire [15:0] A_q, alu_1_y, B_q, counter_1_q, multiplexer_1_out, multiplexer_2_out, multiplexer_4_out,
       ram_1_dout;
  wire [20:0] ProgramROM_data;

  Button RESET (.out(RESET_out));
  Counter #(.max('hffff), .width(16)) counter_1 (
    .clr(RESET_out), .load(jz_control_1_m1), .clk(clock_1_out), .D(ProgramROM_data[15:0]), .Q(counter_1_q));  // open: up, count, carry
  Clock clock_1 (.out(clock_1_out));
  ROM #(.addrWidth(16), .dataWidth(21)) ProgramROM (.addr(counter_1_q), .data(ProgramROM_data));
  jz_control jz_control_1 (.A(A_q), .PC_LOAD(PC_LOAD), .M1(jz_control_1_m1));
  RAM #(.asyncread("true"), .dataWidth(16)) ram_1 (
    .addr(multiplexer_3_out), .we(control_unit_1_mem_write), .oe(control_unit_1_mem_read), .clk(clock_1_out),
    .din(multiplexer_4_out), .dout(ram_1_dout));
  // Probe on ProgramROM_data[15:0]
  control_unit control_unit_1 (
    .OP_CODE(ProgramROM_data[20:16]), .WE_A(control_unit_1_we_a), .WE_B(control_unit_1_we_b),
    .SRC_A(control_unit_1_src_a), .SRC_B(control_unit_1_src_b), .ALU_OP_CODE(control_unit_1_alu_op_code),
    .MEM_READ(control_unit_1_mem_read), .MEM_WRITE(control_unit_1_mem_write),
    .MEM_SRC(control_unit_1_mem_src), .MEM_ADDR_SRC(control_unit_1_mem_addr_src), .PC_LOAD(PC_LOAD));
  Multiplexer #(.select(2), .width(16)) multiplexer_1 (
    .in0(ProgramROM_data[15:0]), .in1(alu_1_y), .in2(ram_1_dout), .out(multiplexer_1_out),
    .sel(control_unit_1_src_a));  // open: in3
  Multiplexer #(.width(16)) multiplexer_2 (
    .in0(ProgramROM_data[15:0]), .in1(ram_1_dout), .out(multiplexer_2_out), .sel(control_unit_1_src_b));
  Register #(.width(16)) A (.D(multiplexer_1_out), .en(control_unit_1_we_a), .clk(clock_1_out), .Q(A_q));  // open: clr
  Register #(.width(16)) B (.D(multiplexer_2_out), .en(control_unit_1_we_b), .clk(clock_1_out), .Q(B_q));  // open: clr
  // Probe on control_unit_1_alu_op_code
  Multiplexer #(.width(16)) multiplexer_3 (
    .in0(ProgramROM_data[15:0]), .in1(B_q), .out({multiplexer_3_out_2, multiplexer_3_out}),
    .sel(control_unit_1_mem_addr_src));
  Multiplexer #(.width(16)) multiplexer_4 (.in0(A_q), .in1(B_q), .out(multiplexer_4_out), .sel(control_unit_1_mem_src));
  // Probe on alu_1_y
  // Probe on A_q
  // Probe on B_q
  alu alu_1 (
    .A(A_q), .B(B_q), .F2(control_unit_1_alu_op_code[2]), .F1(control_unit_1_alu_op_code[1]),
    .F0(control_unit_1_alu_op_code[0]), .Y(alu_1_y));

  // Notes on the sheet:
  //   contents of ProgramROM (hex, n*v repeats v):
  //   1000a c0001 f0001 d0002 110000 10000 100000 100000 a0000
endmodule

module jz_control (
  input  [15:0] A,
  input  PC_LOAD,
  output M1
);

  wire comparator_1_eq;

  Comparator #(.width(16)) comparator_1 (.a(A), .b({16{1'b0}}), .eq(comparator_1_eq));  // open: gt, lt
  and and_1 (M1, comparator_1_eq, PC_LOAD);
endmodule
