// Logisim project OS.circ as structural Verilog: 9 circuits, main circuit main
module alu (
  input  [2:0] F,
  input  [15:0] A,
  input  [15:0] B,
  output [15:0] Y
);

  wire [15:0] adder_1_out, and_1_out, bit_extender_1_out, multiplexer_1_out, not_1_out, or_1_out;

  assign not_1_out = ~B;  // NOT_Gate not_1, 16 bits wide
  Multiplexer #(.width(16)) multiplexer_1 (.in0(B), .in1(not_1_out), .out(multiplexer_1_out), .sel(F[2]));
  Adder #(.width(16)) adder_1 (.a(A), .b(multiplexer_1_out), .out(adder_1_out), .cin(F[2]));  // open: cout
  assign and_1_out = A & multiplexer_1_out;  // AND_Gate and_1, 16 bits wide
  assign or_1_out = A | multiplexer_1_out;  // OR_Gate or_1, 16 bits wide
  assign bit_extender_1_out = {{15{1'b0}}, adder_1_out[15]};  // Bit_Extender bit_extender_1
  Multiplexer #(.select(2), .width(16)) multiplexer_2 (
    .in0(and_1_out), .in1(or_1_out), .in2(adder_1_out), .in3(bit_extender_1_out), .out(Y), .sel(F[1:0]));
endmodule

module control_unit (
  input  [4:0] OP_CODE,
  input  TTY_ADDRESS,
  input  KBD_STATUS_ADDRESS,
  input  KBD_DATA_ADDRESS,
  output WE_A,
  output WE_B,
  output WE_SP,
  output [1:0] SRC_A,
  output SRC_B,
  output SP_INC,
  output [2:0] ALU_OP_CODE,
  output MEM_READ,
  output [1:0] MEM_SRC,
  output MEM_WRITE,
  output [1:0] MEM_ADDR_SRC,
  output [1:0] PC_LOAD,
  output [1:0] PC_SRC,
  output KBD_STATUS_READ,
  output KDB_DATA_READ,
  output TTY_WRITE
);

  wire and_1_out, and_2_out, and_3_out, comparator_1_eq, comparator_2_eq, comparator_3_eq, comparator_4_eq,
       nand_1_out, not_1_out, or_1_out;
  wire [9:8] ControlROM_data;

  Comparator #(.width(5)) comparator_1 (.a(OP_CODE), .b(5'b01100), .eq(comparator_1_eq));  // open: gt, lt
  Comparator #(.width(5)) comparator_2 (.a(OP_CODE), .b(5'b01101), .eq(comparator_2_eq));  // open: gt, lt
  Comparator #(.width(5)) comparator_3 (.a(OP_CODE), .b(5'b01110), .eq(comparator_3_eq));  // open: gt, lt
  Comparator #(.width(5)) comparator_4 (.a(OP_CODE), .b(5'b01111), .eq(comparator_4_eq));  // open: gt, lt
  or or_1 (or_1_out, comparator_1_eq, comparator_2_eq, comparator_3_eq, comparator_4_eq);
  ROM #(.addrWidth(5), .dataWidth(20)) ControlROM (
    .addr(OP_CODE),
    .data({WE_A, WE_B, WE_SP, SRC_A, SRC_B, SP_INC, ALU_OP_CODE, ControlROM_data, MEM_SRC, MEM_ADDR_SRC, PC_LOAD, PC_SRC}));
  and and_1 (and_1_out, or_1_out, TTY_ADDRESS);
  and and_2 (and_2_out, or_1_out, KBD_STATUS_ADDRESS);
  and and_3 (and_3_out, or_1_out, KBD_DATA_ADDRESS);
  nand nand_1 (nand_1_out, and_2_out, and_3_out);
  not not_1 (not_1_out, and_1_out);
  and and_4 (MEM_READ, ControlROM_data[9], nand_1_out);
  and and_5 (KBD_STATUS_READ, ControlROM_data[9], and_2_out);
  and and_6 (KDB_DATA_READ, ControlROM_data[9], and_3_out);
  and and_7 (TTY_WRITE, ControlROM_data[8], and_1_out);
  and and_8 (MEM_WRITE, ControlROM_data[8], not_1_out);

  // Notes on the sheet:
  //   OP_CODE: initial=0x44c
  //   contents of ControlROM (hex, n*v repeats v):
  //   0 80000 40000 88000 88400 88800 89000 89400 89800 89c00 4 7 100 140 90200 44200 90210 110 221a8
  //   202a9 221aa
endmodule

module main (
);

  wire clock_1_out, control_unit_1_p5, control_unit_1_p6, control_unit_1_p8, control_unit_1_p10,
       control_unit_1_p12, control_unit_1_p17, control_unit_1_p18, io_address_decoder_1_kbd_data_address,
       io_address_decoder_1_kbd_status_address, io_address_decoder_1_tty_address, keyboard_1_avail,
       pc_control_1_m1, RESET_out;
  wire [1:0] control_unit_1_p7, control_unit_1_p11, control_unit_1_p13, control_unit_1_p15, PC_LOAD;
  wire [2:0] control_unit_1_p9;
  wire [6:0] keyboard_1_data, multiplexer_4_out;
  wire [7:0] adder_1_out, B_q, B_q_2, multiplexer_3_out, ProgramROM_data, ProgramROM_data_2, SP_q;
  wire [8:0] multiplexer_4_out_2;
  wire [15:0] A_q, alu_1_y, bit_extender_1_out, bit_extender_2_out, counter_1_q, multiplexer_1_out,
       multiplexer_2_out, multiplexer_5_out, ram_1_dout;
  wire [20:16] ProgramROM_data_3;

  Counter #(.max('hffff), .width(16)) counter_1 (
    .clr(RESET_out), .load(pc_control_1_m1), .clk(clock_1_out), .D({ProgramROM_data_2, ProgramROM_data}),
    .Q(counter_1_q));  // open: up, count, carry
  Button RESET (.out(RESET_out));
  Clock clock_1 (.out(clock_1_out));
  ROM #(.addrWidth(16), .dataWidth(21)) ProgramROM (
    .addr(counter_1_q), .data({ProgramROM_data_3, ProgramROM_data_2, ProgramROM_data}));
  Register SP (.D(adder_1_out), .en(control_unit_1_p18), .clk(clock_1_out), .Q(SP_q));  // open: clr
  Adder adder_1 (.a(8'h1), .b(SP_q), .out(adder_1_out));  // open: cin, cout
  pc_control pc_control_1 (.A(A_q), .PC_CTL(PC_LOAD), .M1(pc_control_1_m1));
  io_address_decoder io_address_decoder_1 (
    .ADDRESS({ProgramROM_data_2, ProgramROM_data}), .TTY_ADDRESS(io_address_decoder_1_tty_address),
    .KBD_STATUS_ADDRESS(io_address_decoder_1_kbd_status_address),
    .KBD_DATA_ADDRESS(io_address_decoder_1_kbd_data_address));
  RAM #(.asyncread("true"), .dataWidth(16)) ram_1 (
    .addr(multiplexer_3_out), .we(control_unit_1_p12), .oe(control_unit_1_p10), .clk(clock_1_out),
    .din({multiplexer_4_out_2, multiplexer_4_out}), .dout(ram_1_dout));
  TTY tty_1 (.data(multiplexer_4_out), .clk(clock_1_out), .we(control_unit_1_p17));  // open: clr
  Keyboard keyboard_1 (
    .clk(clock_1_out), .re(control_unit_1_p15[1]), .avail(keyboard_1_avail), .data(keyboard_1_data));  // open: clr
  // control_unit control_unit_1: pin names not known; wires that end beside it: ProgramROM_data_3, io_address_decoder_1_kbd_status_address, io_address_decoder_1_kbd_data_address, io_address_decoder_1_tty_address, control_unit_1_p5, control_unit_1_p6, control_unit_1_p7, control_unit_1_p8, control_unit_1_p9, control_unit_1_p10, control_unit_1_p11, control_unit_1_p12, control_unit_1_p13, PC_LOAD, control_unit_1_p15[0], control_unit_1_p15[1], control_unit_1_p17, control_unit_1_p18
  Multiplexer #(.select(2), .width(16)) multiplexer_1 (
    .in0({ProgramROM_data_2, ProgramROM_data}), .in1(alu_1_y), .in2(multiplexer_5_out),
    .out(multiplexer_1_out), .sel(control_unit_1_p7));  // open: in3
  Multiplexer #(.width(16)) multiplexer_2 (
    .in0({ProgramROM_data_2, ProgramROM_data}), .in1(multiplexer_5_out), .out(multiplexer_2_out),
    .sel(control_unit_1_p8));
  Multiplexer #(.select(2), .width(8)) multiplexer_3 (
    .in0(ProgramROM_data), .in1(B_q), .in2(SP_q), .out(multiplexer_3_out), .sel(control_unit_1_p13));  // open: in3
  Register #(.width(16)) A (.D(multiplexer_1_out), .en(control_unit_1_p5), .clk(clock_1_out), .Q(A_q));  // open: clr
  Register #(.width(16)) B (
    .D(multiplexer_2_out), .en(control_unit_1_p6), .clk(clock_1_out), .Q({B_q_2, B_q}));  // open: clr
  Multiplexer #(.select(2), .width(16)) multiplexer_4 (
    .in0(A_q), .in1({B_q_2, B_q}), .out({multiplexer_4_out_2, multiplexer_4_out}), .sel(control_unit_1_p11));  // open: in2, in3
  assign bit_extender_1_out = {{9{1'b0}}, keyboard_1_data};  // Bit_Extender bit_extender_1
  assign bit_extender_2_out = {{15{1'b0}}, keyboard_1_avail};  // Bit_Extender bit_extender_2
  alu alu_1 (.A(A_q), .B({B_q_2, B_q}), .Y(alu_1_y));  // open: F
  Multiplexer #(.select(2), .width(16)) multiplexer_5 (
    .in0(ram_1_dout), .in1(bit_extender_2_out), .in2(bit_extender_1_out), .out(multiplexer_5_out),
    .sel(control_unit_1_p15));  // open: in3
  // Pins of 1 and 2 bits meet at PC_LOAD

  // Notes on the sheet:
  //   contents of ProgramROM (hex, n*v repeats v):
  //   e0102 a0000 e0101 c0100 10000 a0000
endmodule

module pc_control (
  input  [15:0] A,
  input  [1:0] PC_CTL,
  output M1
);

  wire and_1_out, and_2_out, comparator_1_eq, not_1_out, not_2_out;

  Comparator #(.width(16)) comparator_1 (.a(A), .b({16{1'b0}}), .eq(comparator_1_eq));  // open: gt, lt
  not not_1 (not_1_out, PC_CTL[0]);
  not not_2 (not_2_out, PC_CTL[1]);
  and and_1 (and_1_out, comparator_1_eq, PC_CTL[0], not_2_out);
  and and_2 (and_2_out, not_1_out, PC_CTL[1]);
  or or_1 (M1, and_1_out, and_2_out);
endmodule

module io_address_decoder (
  input  [15:0] ADDRESS,
  output TTY_ADDRESS,
  output KBD_STATUS_ADDRESS,
  output KBD_DATA_ADDRESS
);

  Comparator #(.width(9)) comparator_1 (.a(ADDRESS[8:0]), .b(9'h100), .eq(TTY_ADDRESS));  // open: gt, lt
  Comparator #(.width(9)) comparator_2 (.a(ADDRESS[8:0]), .b(9'h102), .eq(KBD_STATUS_ADDRESS));  // open: gt, lt
  Comparator #(.width(9)) comparator_3 (.a(ADDRESS[8:0]), .b(9'h101), .eq(KBD_DATA_ADDRESS));  // open: gt, lt
endmodule

module test (
);

  wire clock_1_out;
  wire [7:0] register_1_q;

  Clock clock_1 (.out(clock_1_out));
  Counter counter_1 (.clk(clock_1_out));  // open: clr, load, up, count, D, carry, Q
  Register register_1 (.clk(clock_1_out), .Q(register_1_q));  // open: D, en, clr
  RAM ram_1 (.addr(register_1_q), .clk(clock_1_out));  // open: we, oe, din, dout
endmodule

module new_main (
);

  wire clock_1_out, control_unit_1_mem_read, control_unit_1_mem_write, control_unit_1_sp_inc,
       control_unit_1_src_b, control_unit_1_tty_write, control_unit_1_we_a, control_unit_1_we_b,
       control_unit_1_we_sp, io_address_decoder_1_kbd_data_address, io_address_decoder_1_kbd_status_address,
       io_address_decoder_1_tty_address, keyboard_1_avail, pc_control_1_m1, RESET_out, RRR_out, undriven,
       undriven_2;
  wire [1:0] control_unit_1_kbd_status_read, control_unit_1_mem_addr_src, control_unit_1_mem_src,
       control_unit_1_pc_load, control_unit_1_pc_src, control_unit_1_src_a;
  wire [2:0] control_unit_1_alu_op_code;
  wire [6:0] keyboard_1_data, multiplexer_7_out;
  wire [7:0] adder_1_out, B_q, B_q_2, multiplexer_2_out, multiplexer_4_out, ProgramROM_data,
       ProgramROM_data_2, register_1_q, sp_1_sp_val, subtractor_1_out;
  wire [8:0] multiplexer_7_out_2;
  wire [15:0] A_q, adder_2_out, alu_1_y, bit_extender_1_out, bit_extender_2_out, counter_1_q,
       multiplexer_1_out, multiplexer_3_out, multiplexer_5_out, multiplexer_6_out, ram_1_dout;
  wire [20:16] ProgramROM_data_3;

  pc_control pc_control_1 (.A(A_q), .PC_CTL(control_unit_1_pc_load), .M1(pc_control_1_m1));
  Counter #(.max('hffff), .ongoal("stay"), .width(16)) counter_1 (
    .clr(RESET_out), .load(pc_control_1_m1), .clk(clock_1_out), .D(multiplexer_1_out), .Q(counter_1_q));  // open: up, count, carry
  Multiplexer #(.select(2), .width(16)) multiplexer_1 (
    .in0({ProgramROM_data_2, ProgramROM_data}), .in1(ram_1_dout), .in2(A_q), .in3({B_q_2, B_q}),
    .out(multiplexer_1_out), .sel(control_unit_1_pc_src));
  Button RESET (.out(RESET_out));
  io_address_decoder io_address_decoder_1 (
    .ADDRESS({ProgramROM_data_2, ProgramROM_data}), .TTY_ADDRESS(io_address_decoder_1_tty_address),
    .KBD_STATUS_ADDRESS(io_address_decoder_1_kbd_status_address),
    .KBD_DATA_ADDRESS(io_address_decoder_1_kbd_data_address));
  TTY tty_1 (.data(multiplexer_7_out), .clk(clock_1_out), .we(control_unit_1_tty_write));  // open: clr
  Keyboard #(.buflen(16)) keyboard_1 (
    .clk(clock_1_out), .re(control_unit_1_kbd_status_read[1]), .avail(keyboard_1_avail),
    .data(keyboard_1_data));  // open: clr
  ROM #(.addrWidth(16), .dataWidth(21)) ProgramROM (
    .addr(counter_1_q), .data({ProgramROM_data_3, ProgramROM_data_2, ProgramROM_data}));
  control_unit control_unit_1 (
    .OP_CODE(ProgramROM_data_3), .TTY_ADDRESS(io_address_decoder_1_tty_address),
    .KBD_STATUS_ADDRESS(io_address_decoder_1_kbd_status_address),
    .KBD_DATA_ADDRESS(io_address_decoder_1_kbd_data_address), .WE_A(control_unit_1_we_a),
    .WE_B(control_unit_1_we_b), .WE_SP(control_unit_1_we_sp), .SRC_A(control_unit_1_src_a),
    .SRC_B(control_unit_1_src_b), .SP_INC(control_unit_1_sp_inc), .ALU_OP_CODE(control_unit_1_alu_op_code),
    .MEM_READ(control_unit_1_mem_read), .MEM_SRC(control_unit_1_mem_src),
    .MEM_WRITE(control_unit_1_mem_write), .MEM_ADDR_SRC(control_unit_1_mem_addr_src),
    .PC_LOAD(control_unit_1_pc_load), .PC_SRC(control_unit_1_pc_src),
    .KBD_STATUS_READ(control_unit_1_kbd_status_read[0]), .KDB_DATA_READ(control_unit_1_kbd_status_read[1]),
    .TTY_WRITE(control_unit_1_tty_write));
  sp sp_1 (.SP_INC(control_unit_1_sp_inc), .SP_WE(control_unit_1_we_sp), .CLOCK(clock_1_out), .SP_VAL(sp_1_sp_val));
  Clock clock_1 (.out(clock_1_out));
  Button RRR (.out(RRR_out));
  Multiplexer #(.width(8)) multiplexer_2 (
    .in0(subtractor_1_out), .in1(adder_1_out), .out(multiplexer_2_out), .sel(undriven_2));
  Register register_1 (.D(multiplexer_2_out), .en(undriven), .clk(clock_1_out), .Q(register_1_q));  // open: clr
  assign bit_extender_1_out = {{15{1'b0}}, keyboard_1_avail};  // Bit_Extender bit_extender_1
  assign bit_extender_2_out = {{9{1'b0}}, keyboard_1_data};  // Bit_Extender bit_extender_2
  Multiplexer #(.select(2), .width(16)) multiplexer_3 (
    .in0(ram_1_dout), .in1(bit_extender_1_out), .in2(bit_extender_2_out), .out(multiplexer_3_out),
    .sel(control_unit_1_kbd_status_read));  // open: in3
  Multiplexer #(.select(2), .width(8)) multiplexer_4 (
    .in0(ProgramROM_data), .in1(B_q), .in2(sp_1_sp_val), .out(multiplexer_4_out),
    .sel(control_unit_1_mem_addr_src));  // open: in3
  // Probe on {multiplexer_7_out_2, multiplexer_7_out}
  Subtractor subtractor_1 (.a(register_1_q), .b(8'h1), .out(subtractor_1_out));  // open: bin, bout
  Adder adder_1 (.a(8'h1), .b(register_1_q), .out(adder_1_out));  // open: cin, cout
  // Probe on multiplexer_5_out
  Multiplexer #(.select(2), .width(16)) multiplexer_5 (
    .in0({ProgramROM_data_2, ProgramROM_data}), .in1(alu_1_y), .in2(multiplexer_3_out),
    .out(multiplexer_5_out), .sel(control_unit_1_src_a));  // open: in3
  // Probe on multiplexer_6_out
  Multiplexer #(.width(16)) multiplexer_6 (
    .in0({ProgramROM_data_2, ProgramROM_data}), .in1(multiplexer_3_out), .out(multiplexer_6_out),
    .sel(control_unit_1_src_b));
  Adder #(.width(16)) adder_2 (.a(counter_1_q), .b(16'h1), .out(adder_2_out));  // open: cin, cout
  // Probe on multiplexer_4_out
  RAM #(.asyncread("true"), .dataWidth(16)) ram_1 (
    .addr(multiplexer_4_out), .we(control_unit_1_mem_write), .oe(control_unit_1_mem_read), .clk(clock_1_out),
    .din({multiplexer_7_out_2, multiplexer_7_out}), .dout(ram_1_dout));
  Register #(.width(16)) A (.D(multiplexer_5_out), .en(control_unit_1_we_a), .clk(clock_1_out), .Q(A_q));  // open: clr
  Register #(.width(16)) B (
    .D(multiplexer_6_out), .en(control_unit_1_we_b), .clk(clock_1_out), .Q({B_q_2, B_q}));  // open: clr
  Multiplexer #(.select(2), .width(16)) multiplexer_7 (
    .in0(A_q), .in1({B_q_2, B_q}), .in2(adder_2_out), .out({multiplexer_7_out_2, multiplexer_7_out}),
    .sel(control_unit_1_mem_src));  // open: in3
  // Probe on A_q
  // Probe on {B_q_2, B_q}
  alu alu_1 (.A(A_q), .B({B_q_2, B_q}), .F(control_unit_1_alu_op_code), .Y(alu_1_y));

  // Notes on the sheet:
  //   contents of ProgramROM (hex, n*v repeats v):
  //   af000 255*0 1006f c00be 10064 c00bf 10064 c00c0 1006f c00c1 10072 c00c2 10065 c00c3 10076 c00c4
  //   10065 c00c5 1006e c00c6 1000a c00c7 10550 c00c8 10068 c00c9 10069 c00ca 1000a c00cb 10600 c00cc
  //   1000a c00cd 130000 735*0 e00bd 200fe 90000 130000 f00bd 100000 2000a 80000 130000 e00bd 20001 50000
  //   c00bd 130000 100f0 c00bd e0102 a0410 e0101 f00bd 110000 120400 a041c 120404 a041c 120409 10000 a0410
  //   130000 100f0 c00bd f00bd 100000 c0100 120400 a0429 120404 a0429 120409 10000 a041f 130000 12040e
  //   100f0 c00bd 10000 c00bc 120400 a044a 120404 a044a e00bc a0440 f00bc 9*50000 c00bc f00bd 100000 20030
  //   80000 f00bc 50000 c00bc 120409 10000 a042f e00bc 130000 e00bc 130000 178*0 100be c00bd 100f0 c00bc
  //   f00bd 100000 c00bb f00bc 100000 f00bb 80000 a0519 120525 12052f a0511 10000 a050c 120525 120525
  //   12052f a0523 100f0 c00bc 10000 a0504 12052f a051f 120525 12052a 10000 a0504 120525 f00bd 100000
  //   130000 10000 130000 e00bd 20001 50000 c00bd 130000 e00bc 20001 50000 c00bc 130000 f00bd 100000 2000a
  //   80000 130000 28*0 10050 c0100 1006c c0100 10065 c0100 10061 c0100 10073 c0100 10065 c0100 10020
  //   c0100 10065 c0100 1006e c0100 10074 c0100 10065 c0100 10072 c0100 10020 c0100 10061 c0100 10020
  //   c0100 1006e c0100 10075 c0100 1006d c0100 10062 c0100 10065 c0100 10072 c0100 1003a c0100 1000a
  //   c0100 12042a 12041d 20001 30000 a05ab 10054 c0100 10068 c0100 10065 c0100 10020 c0100 1006e c0100
  //   10075 c0100 1006d c0100 10062 c0100 10065 c0100 10072 c0100 10020 c0100 10069 c0100 10073 c0100
  //   10020 c0100 10065 c0100 10076 c0100 10065 c0100 1006e c0100 1002e c0100 1000a c0100 10054 c0100
  //   10068 c0100 10065 c0100 10020 c0100 1006e c0100 10075 c0100 1006d c0100 10062 c0100 10065 c0100
  //   10072 c0100 10020 c0100 10069 c0100 10073 c0100 10020 c0100 1006f c0100 10064 c0100 10064 c0100
  //   1002e c0100 1000a c0100 10000 a05d3 130000 44*0 10050 c0100 1006c c0100 10065 c0100 10061 c0100
  //   10073 c0100 10065 c0100 10020 c0100 10074 c0100 10079 c0100 10070 c0100 10065 c0100 10020 c0100
  //   10079 c0100 1006f c0100 10075 c0100 10072 c0100 10020 c0100 1006e c0100 10061 c0100 1006d c0100
  //   10065 c0100 1000a c0100 12040e 10048 c0100 10065 c0100 1006c c0100 1006c c0100 1006f c0100 1002c
  //   c0100 10020 c0100 12041d 130000 59843*0 120100 10048 c0100 10069 c0100 1002c c0100 10020 c0100 10049
  //   c0100 10020 c0100 10061 c0100 1006d c0100 10020 c0100 10074 c0100 10069 c0100 1006e c0100 10079
  //   c0100 1004f c0100 10053 c0100 1002e c0100 1000a c0100 10050 c0100 1006c c0100 10065 c0100 10061
  //   c0100 10073 c0100 10065 c0100 10020 c0100 1006e c0100 10061 c0100 1006d c0100 10065 c0100 10020
  //   c0100 10061 c0100 10020 c0100 10070 c0100 10072 c0100 1006f c0100 10067 c0100 10072 c0100 10061
  //   c0100 1006d c0100 10020 c0100 10079 c0100 1006f c0100 10075 c0100 10020 c0100 10077 c0100 10061
  //   c0100 1006e c0100 10074 c0100 10020 c0100 10074 c0100 1006f c0100 10020 c0100 10072 c0100 10075
  //   c0100 1006e c0100 1002e c0100 1000a c0100 10041 c0100 10076 c0100 10061 c0100 10069 c0100 1006c
  //   c0100 10061 c0100 10062 c0100 1006c c0100 10065 c0100 10020 c0100 10070 c0100 10072 c0100 1006f
  //   c0100 10067 c0100 10072 c0100 10061 c0100 1006d c0100 10073 c0100 1003a c0100 1000a c0100 1006f
  //   c0100 10064 c0100 10064 c0100 1006f c0100 10072 c0100 10065 c0100 10076 c0100 10065 c0100 1006e
  //   c0100 1000a c0100 10068 c0100 10069 c0100 1000a c0100 12040e 120500 af0b9 140000 10000 af023 1004e
  //   c0100 1006f c0100 10020 c0100 10073 c0100 10075 c0100 10063 c0100 10068 c0100 10020 c0100 10070
  //   c0100 10072 c0100 1006f c0100 10067 c0100 10072 c0100 10061 c0100 1006d c0100 10020 c0100 10065
  //   c0100 10078 c0100 10069 c0100 10073 c0100 10074 c0100 10073 c0100 1000a c0100 10000 af023
endmodule

module main_debug (
);

  wire clock_1_out, control_unit_1_kbd_status_read, control_unit_1_kdb_data_read, keyboard_1_p1,
       keyboard_1_p3, RESET_out, undriven_3, undriven_4, undriven_5;
  wire [1:0] control_unit_1_pc_src;
  wire [6:0] undriven_6;
  wire [7:0] adder_1_out, multiplexer_1_out, SP_q, undriven_7, undriven_8;
  wire [15:0] ram_1_dout, undriven, undriven_2, undriven_9;
  wire [20:0] ProgramROM_data;

  Counter #(.max('hffff), .width(16)) counter_1 (
    .clr(RESET_out), .clk(clock_1_out), .D(undriven));  // open: load, up, count, carry, Q
  Button RESET (.out(RESET_out));
  Clock clock_1 (.out(clock_1_out));
  ROM #(.addrWidth(16), .dataWidth(21)) ProgramROM (.addr(undriven_2), .data(ProgramROM_data));
  Register SP (.D(adder_1_out), .en(control_unit_1_kbd_status_read), .clk(clock_1_out), .Q(SP_q));  // open: clr
  Adder adder_1 (.a(8'h1), .b(SP_q), .out(adder_1_out));  // open: cin, cout
  pc_control pc_control_1 ();  // open: A, PC_CTL, M1
  io_address_decoder io_address_decoder_1 ();  // open: ADDRESS, TTY_ADDRESS, KBD_STATUS_ADDRESS, KBD_DATA_ADDRESS
  RAM #(.asyncread("true"), .dataWidth(16)) ram_1 (
    .addr(multiplexer_1_out), .clk(clock_1_out), .dout(ram_1_dout));  // open: we, oe, din
  TTY tty_1 (.data(undriven_6), .clk(clock_1_out), .we(keyboard_1_p1));  // open: clr
  // Keyboard keyboard_1: pin names not known; wires that end beside it: keyboard_1_p1, clock_1_out, keyboard_1_p3, keyboard_1_p3
  control_unit control_unit_1 (
    .TTY_ADDRESS(undriven_4), .KBD_STATUS_ADDRESS(undriven_3), .KBD_DATA_ADDRESS(undriven_5),
    .PC_SRC(control_unit_1_pc_src), .KBD_STATUS_READ(control_unit_1_kbd_status_read),
    .KDB_DATA_READ(control_unit_1_kdb_data_read));  // open: OP_CODE, WE_A, WE_B, WE_SP, SRC_A, SRC_B, SP_INC, ALU_OP_CODE, MEM_READ, MEM_SRC, MEM_WRITE, MEM_ADDR_SRC, PC_LOAD, TTY_WRITE
  Multiplexer #(.select(2), .width(8)) multiplexer_1 (
    .in0(undriven_7), .in1(undriven_8), .in2(SP_q), .out(multiplexer_1_out));  // open: in3, sel
  Register #(.width(16)) A (.D(undriven_9), .clk(clock_1_out));  // open: en, Q, clr
  Register #(.width(16)) B (.clk(clock_1_out));  // open: D, en, Q, clr
  alu alu_1 ();  // open: A, B, F, Y

  // Notes on the sheet:
  //   contents of ProgramROM (hex, n*v repeats v):
  //   e0102 a0000 e0101 c0100 10000 a0000
endmodule

module sp (
  input  SP_INC,
  input  SP_WE,
  input  CLOCK,
  output [7:0] SP_VAL
);

  wire [7:0] adder_1_out, multiplexer_1_out, SP_q, subtractor_1_out;

  Multiplexer #(.width(8)) multiplexer_1 (
    .in0(subtractor_1_out), .in1(adder_1_out), .out(multiplexer_1_out), .sel(SP_INC));
  Register SP (.D(multiplexer_1_out), .en(SP_WE), .clk(CLOCK), .Q(SP_q));  // open: clr
  Subtractor subtractor_1 (.a(SP_q), .b(8'h1), .out(subtractor_1_out));  // open: bin, bout
  Adder adder_1 (.a(8'h1), .b(SP_q), .out(adder_1_out));  // open: cin, cout
  Multiplexer #(.width(8)) multiplexer_2 (.in0(multiplexer_1_out), .in1(SP_q), .out(SP_VAL), .sel(SP_INC));
endmodule
